# Fritzing sketch NRFTransmitter (saved by Fritzing 0.9.3b)

parts:
  Part3 = Arduino Pro Mini v13
  Part4 = NRF24L01+ Breakout Board
  R1 = Photocell (LDR) [package=THT]
  R2 = Resistor [tolerance=±5% resistance=220 package=THT]
  LED1 = LED - 5mm [color="Red (633nm)" package="5 mm [THT]"]  # not connected
  VCC1 = Battery block 9V  # not connected

nets:
  VCC: Part3.A5, Part3.VCC, Part4.VCC, R1.pin_0
  GND: Part3.GND, Part4.GND, R2.Pin_1
  N1: Part3.A1, R1.pin_1, R2.Pin_0
  N2: Part3.D13/SCK, Part4.SCK
  N3: Part3.D12/MISO, Part4.MISO
  N4: Part3.D11_PWM/MOSI, Part4.MOSI
  N5: Part3.D8, Part4.CS
  N6: Part3.D7, Part4.CE

notes:
  Laser Transimitter
  Laser Reciever and Signal Transmitter
