# Fritzing sketch nrfReciever (saved by Fritzing 0.9.3b)

parts:
  Part1 = Arduino Pro Mini v13
  Part2 = NRF24L01+ Breakout Board
  R1 = Resistor [tolerance=±5% resistance=220 package="0603 [SMD]"]
  S1 = Momentary Switch [package=ksa_sealed_tac_switch]
  LED1 = LED - 5mm [color="Red (633nm)" package="5 mm [THT]"]
  J1 = Piezo Speaker

nets:
  GND: Part1.GND, Part2.GND, R1.Pin_1, LED1.cathode, J1.pin1
  VCC: Part1.VCC, Part2.VCC, S1.4
  N1: Part1.D13/SCK, Part2.SCK
  N2: Part1.D12/MISO, Part2.MISO
  N3: Part1.D11_PWM/MOSI, Part2.MOSI
  N4: Part1.D8, Part2.CS
  N5: Part1.D7, Part2.CE
  N6: Part1.D3_PWM, R1.Pin_0, S1.2
  N7: Part1.D2, LED1.anode, J1.pin2

notes:
  Signal Reciever
